# Fritzing sketch FINAL circuit design (saved by Fritzing 0.9.3b)

parts:
  Driver2 = 28BYJ-48 Driver Module [part_number=ULN2003 package=THT]
  SM2 = 28BYJ-48 Stepper Motor [part_number=28BYJ-48]
  YL-83_-_Control_Board3 = YL-83 Rain Sensor - Control Board
  YL-83_-_Detection_Board3 = YL-83 Rain Sensor - Detection Board
  BAT1 = BC9VPC [package=bc9vpc]
  Part1 = Arduino Uno (Rev3)

nets:
  N1: Driver2.IN1, Part1.D8
  N2: Driver2.IN2, Part1.D9_PWM
  N3: Driver2.IN3, Part1.D10_PWM/SS
  N4: Driver2.IN4, Part1.D11_PWM/MOSI
  N5: Driver2.GND, BAT1.V-
  N6: Driver2.Vmotor, BAT1.V+
  N7: Driver2.blue-pin, SM2.blue-pin
  N8: Driver2.pink-pin, SM2.pink-pin
  N9: Driver2.yellow-pin, SM2.yellow-pin
  N10: Driver2.orange-pin, SM2.orange-pin
  N11: Driver2.red-pin, SM2.red-pin
  VCC: YL-83_-_Control_Board3.VCC, Part1.5V
  GND: YL-83_-_Control_Board3.GND, Part1.GND
  N12: YL-83_-_Control_Board3.DO, Part1.D2
  N13: YL-83_-_Control_Board3.POS, YL-83_-_Detection_Board3.POS
  N14: YL-83_-_Control_Board3.NEG, YL-83_-_Detection_Board3.NEG

custom parts:
  28BYJ-48 Driver Module: Generic male header
  28BYJ-48 Stepper Motor: Unipolar Stepper Motor 28BYJ-48 Top coil - pink & orange Bottom coil - blue & yellow Common rail - red Connector pins: blue - pink - yellow - orange - red
  YL-83 Rain Sensor - Control Board: The YL-83 is a rain sensor that has more resistance when dry and less resistance when wet. The module runs at 5V.
  YL-83 Rain Sensor - Detection Board: The YL-83 is a rain sensor that has more resistance when dry and less resistance when wet. The module runs at 5V.
